// Logisim project сумматор одноразрядный.circ as structural Verilog: 1 circuit, main circuit main
module main (
  input  A,
  input  B,
  input  C,
  output Perenos,
  output Sum
);

  wire and_1_out, and_2_out, and_3_out, and_4_out, and_5_out, and_6_out, and_7_out, not_1_out, not_2_out,
       not_3_out, not_4_out, not_5_out, not_6_out;

  not not_1 (not_1_out, B);
  not not_2 (not_2_out, C);
  not not_3 (not_3_out, A);
  not not_4 (not_4_out, C);
  not not_5 (not_5_out, A);
  not not_6 (not_6_out, B);
  and and_1 (and_1_out, A, C);
  and and_2 (and_2_out, A, B);
  and and_3 (and_3_out, B, C);
  or or_1 (Perenos, and_1_out, and_2_out, and_3_out);
  and and_4 (and_4_out, A, not_1_out, not_2_out);
  and and_5 (and_5_out, not_3_out, B, not_4_out);
  and and_6 (and_6_out, not_5_out, not_6_out, C);
  and and_7 (and_7_out, A, B, C);
  or or_2 (Sum, and_4_out, and_5_out, and_6_out, and_7_out);
endmodule
