// Logisim project automat4.circ as structural Verilog: 1 circuit, main circuit main
module main (
  output [3:0] out_1
);

  wire and_1_out, and_2_out, clock_1_out, not_1_out, not_2_out, not_3_out;

  Clock clock_1 (.out(clock_1_out));
  T_Flip_Flop t_ff_1 (.clk(clock_1_out), .T(1'b1), .Q(out_1[0]));  // open: Qn, preset, reset, en
  // Probe on out_1
  not not_1 (not_1_out, out_1[0]);
  not not_2 (not_2_out, out_1[1]);
  T_Flip_Flop t_ff_2 (.clk(clock_1_out), .T(not_1_out), .Q(out_1[1]));  // open: Qn, preset, reset, en
  and and_1 (and_1_out, not_2_out, not_1_out);
  T_Flip_Flop t_ff_3 (.clk(clock_1_out), .T(and_1_out), .Q(out_1[2]));  // open: Qn, preset, reset, en
  not not_3 (not_3_out, out_1[2]);
  and and_2 (and_2_out, not_3_out, and_1_out);
  T_Flip_Flop t_ff_4 (.clk(clock_1_out), .T(and_2_out), .Q(out_1[3]));  // open: Qn, preset, reset, en
endmodule
